# Fritzing sketch Circuito VLC (saved by Fritzing 1.0.2b)
circuit board: 2.12242cm x 1.90681cm
circuit board: 1.68849cm x 2.02648cm

parts:
  Arduino_Emisor = Arduino Uno (Rev3)
  LED1 = LED - 5mm [color="Red (633nm)" current=0.030A package="5 mm [THT]"]
  R1 = Resistor [tolerance=±5% power=0.25W resistance=220 package=THT]
  Arduino_Receptor = Arduino Uno (Rev3)
  R2 = Resistor [tolerance=±5% power=0.25W resistance=50k package=THT]
  Photodiode1 = S1133 Si Photodiode [package="8mm Ceramic [THT]"]

nets:
  N1: Arduino_Emisor.D13/SCK, LED1.anode
  N2: Arduino_Emisor.GND, R1.Pin_1
  N3: LED1.cathode, R1.Pin_0
  N4: Arduino_Receptor.A0, R2.Pin_0, Photodiode1.anode
  N5: Arduino_Receptor.5V, Photodiode1.cathode
  N6: Arduino_Receptor.GND, R2.Pin_1
